# Fritzing sketch esp-desk-util (saved by Fritzing 0.9.5d)

parts:
  esp1 = ESP32 DevKitc V4
  OLED_I2C1 = OLED 128x64 I2C Monochrome Display
  Sensor1 = TTP223B Capacitive Touch Sensor Module
  U1 = WS2812 RGB LED strip
  U2 = Micro USB B Connectors DIP [package=usb-ab-micro-smd]
  J2 = male pin header, 5 pins [form="♂ (male)"]
  J1 = male pin header, 4 pins [form="♂ (male)"]
  M1 = BME280

nets:
  N1: esp1.IO16, OLED_I2C1.SDA
  N2: esp1.IO17, OLED_I2C1.SCK
  N3: esp1.IO18, M1.SDA
  N4: esp1.IO19, M1.SCL
  N5: esp1.IO21, Sensor1.SIG
  N6: esp1.IO22, U1.DIN
  N7: esp1.3V3, J1.pin1
  N8: esp1.GND, J2.pin1
  N9: OLED_I2C1.VDD, J1.pin3
  N10: OLED_I2C1.GND, J2.pin3
  N11: Sensor1.GND, J2.pin4
  N12: Sensor1.VCC, J1.pin4
  GND: U1.GND, U2.GND, J2.pin5
  N13: U1.VCC, U2.VBUS
  N14: J2.pin2, M1.GND
  N15: J1.pin2, M1.VIN

custom parts:
  ESP32 DevKitc V4: ESP32-DevKitC board with ESP32-WROOM-32 module. ESP32-DevKitC V4 is a small-sized ESP32-based development board produced by Espressif. Most of the pins on the ESP module are broken out to the pin headers on the board. The pins D0, D1, D2, D3, CMD and CLK are used internally for communication between ESP32 and SPI flash memory. They are grouped on both sides near the USB connector. Avoid using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
  TTP223B Capacitive Touch Sensor Module: The TTP223B capacitive touch sensor module uses the TTP223B IC. The appropriate voltage is approximately 2 to 5.5 volts.
  WS2812 RGB LED strip: WS2812 strip
  Micro USB B Connectors DIP: USB Connectors AE-USB-MICRO-B-D K-06656
  BME280: Temperature Humidity Barometric presure Sensor
